# Fritzing sketch skatebord (saved by Fritzing 0.9.3b)

parts:
  Часть1 = Arduino Uno (Rev3)
  U1 = LIPO-2000mAh [package=lipo-2000]
  U2 = LIPO-2000mAh [package=lipo-2000]
  U3 = LIPO-2000mAh [package=lipo-2000]
  Часть2 = Bluetooth HC-05 Macho
  R1 = Resistor [tolerance=±5% resistance=10k package=THT]
  R2 = Resistor [tolerance=±5% resistance=100 package=THT]
  Q1 = Basic FET N-Channel [package="TO220 [THT]"]
  Q2 = Basic FET N-Channel [package="TO220 [THT]"]
  R3 = Resistor [tolerance=±5% resistance=10k package=THT]
  R4 = Resistor [tolerance=±5% resistance=100 package=THT]
  Q3 = Basic FET N-Channel [package="TO220 [THT]"]
  R5 = Resistor [tolerance=±5% resistance=10k package=THT]
  R6 = Resistor [tolerance=±5% resistance=100 package=THT]
  LED1 = LED - 3mm [color="Red (633nm)" package="3 mm [THT]"]
  LED2 = LED - 3mm [color="Blue (430nm)" package="3 mm [THT]"]
  LED3 = LED - 3mm [color="Green (555nm)" package="3 mm [THT]"]

nets:
  N1: Часть1.D8, Часть2.TXD
  N2: Часть1.D9_PWM, R6.Pin_0
  N3: Часть1.D10_PWM/SS, R4.Pin_0
  N4: Часть1.D11_PWM/MOSI, R2.Pin_0
  N5: Часть1.D7, Часть2.RXD
  5V: Часть1.5V, Часть2.VCC
  GND: Часть1.GND, U2.-, Часть2.GND
  N6: Часть1.VIN, U3.+
  N7: U1.+, U3.-, LED1.anode, LED2.anode, LED3.anode
  N8: U1.-, U2.+
  N9: R1.Pin_0, Q1.source
  N10: R1.Pin_1, Q1.gate
  N11: Q1.drain, LED2.cathode
  N12: Q2.gate, R3.Pin_1, R4.Pin_1
  N13: Q2.drain, LED3.cathode
  N14: Q2.source, R3.Pin_0
  N15: Q3.gate, R5.Pin_1, R6.Pin_1
  N16: Q3.drain, LED1.cathode
  N17: Q3.source, R5.Pin_0
